# Fritzing sketch Top Feb 2021 (saved by Fritzing 0.9.3b)
circuit board: 5.62153cm x 2.65916cm
breadboards: 1

parts:
  LLC1 = Logic Level Converter [package="Breakout board"]
  Part1 = Adafruit I2S Mic - SPH0645 [part_number="Adafruit #3421"]
  J1 = Raspberry Pi Header 40pin [package=THT]
  LED = male pin header, 3 pins [form="♂ (male)"]
  Serial = double row male pin header, 2 pins [form="♂ (male)"]
  Mics = Adafruit I2S Mic - SPH0645 [part_number="Adafruit #3421"]
  LLC_Ext = male pin header, 6 pins [form="♂ (male)"]
  Bzz = Piezo Speaker
  PWR = double row male pin header, 2 pins [form="♂ (male)"]
  Sw = double row male pin header, 2 pins [form="♂ (male)"]
  Motion = male pin header, 3 pins [form="♂ (male)"]

nets:
  N1: LLC1.LV1, J1.IO12, LLC_Ext.pin6
  VDD: LLC1.LV, Part1.VDD, Part1.SELECT, J1.3V3, Mics.VDD, LLC_Ext.pin4
  GND: LLC1.L-GND, LLC1.H-GND, Part1.GND, J1.GND, LED.pin3, Mics.GND, Mics.SELECT, LLC_Ext.pin3, Bzz.pin2, PWR.pin2, Sw.pin2, Motion.pin3
  N2: LLC1.LV3, J1.IO14, LLC_Ext.pin2
  N3: LLC1.LV4, J1.IO15, LLC_Ext.pin1
  N4: LLC1.HV4, Serial.pin2
  N5: LLC1.HV3, Serial.pin1
  N6: LLC1.HV, J1.5V, LED.pin2, PWR.pin1, Motion.pin1
  N7: LLC1.HV1, LED.pin1
  N8: Part1.BCLK, J1.IO18, Mics.BCLK
  N9: Part1.DATA, J1.IO20, Mics.DATA
  N10: Part1.WS, J1.IO19, Mics.WS
  N11: J1.IO22#12, Bzz.pin1
  N12: J1.IO13, Motion.pin2
  N13: J1.IO26, Sw.pin1

custom parts:
  Logic Level Converter: 5V to/from 3.3V logic level converter
  Adafruit I2S Mic - SPH0645: For many microcontrollers, adding audio input is easy with one of our analog microphone breakouts. But as you get to bigger and better microcontrollers and microcomputers, you'll find that you don't always have an analog input, or maybe you want to avoid the noise that can seep in with an analog mic system. Once you get past 8-bit micros, you will often find an I2S peripheral, that can take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
  Raspberry Pi Header 40pin: Raspberry Pi 40 pin header - for creating your own shields. (Mar 2020, bb: make breadboard friendly (.4in pin spacing) and add labels. Schematic add labels. PCB make oblong pins to allow routing traces between the pins.)
