# Fritzing sketch circuit v2 (saved by Fritzing 0.9.3b)
breadboards: 1

parts:
  Raspberry_Pi_1 = Raspberry Pi 3 [part_number=RPI-3-V1.2]
  2x_18650_(7_4v) = 18650 battery holder [package=battery-18650-kit]
  DC-_5v_DC = RioRand LM2596
  7_4v_mains = Header 2 [package=screwterminal-3.5mm-2_lock]
  POW_SW = SWITCH-DPDT [package=eg2211]
  RGB_LED = RGB LED (com. cathode, rgb) [package="5 mm [THT]"]
  PAN = Basic Servo
  TILT = Basic Servo
  BOUNCE = Basic Servo
  MOTION_SW = SWITCH-DPDT [package=eg2211]
  Motion_Sns = RCWL-0516 Microwave Radar Motion Sensor Module
  330uF = Capacitor Polarized [package=en_j2]

nets:
  3V3: Raspberry_Pi_1.3v3, Raspberry_Pi_1.3V3, MOTION_SW.1
  N1: Raspberry_Pi_1.GPIO3, MOTION_SW.2
  GND: Raspberry_Pi_1.GND, DC-_5v_DC.Pin_4, RGB_LED.common_cathode, PAN.gnd, TILT.gnd, BOUNCE.gnd, Motion_Sns.GND, 330uF.-
  N2: Raspberry_Pi_1.GPIO17, PAN.pulse
  N3: Raspberry_Pi_1.GPIO27, TILT.pulse
  N4: Raspberry_Pi_1.GPIO22, BOUNCE.pulse
  N5: Raspberry_Pi_1.GPIO5, RGB_LED.blue_anode
  N6: Raspberry_Pi_1.GPIO6, RGB_LED.green_anode
  N7: Raspberry_Pi_1.GPIO13, RGB_LED.red_anode
  VCC: Raspberry_Pi_1.5V, DC-_5v_DC.Pin_3, POW_SW.2, PAN.vcc, TILT.vcc, BOUNCE.vcc, Motion_Sns.VIN, 330uF.+
  N8: 2x_18650_(7_4v).+, POW_SW.6
  N9: 2x_18650_(7_4v).-, DC-_5v_DC.Pin_2, 7_4v_mains.1
  N10: DC-_5v_DC.Pin_1, POW_SW.5
  N11: 7_4v_mains.2, POW_SW.4
  N12: MOTION_SW.3, Motion_Sns.OUT

notes:
  V2.0 2019-08-24

custom parts:
  18650 battery holder: 18650 Battery Holder
  RCWL-0516 Microwave Radar Motion Sensor Module: The RCWL-0516 is a microwave radar motion sensor module. Input voltage is 4V to 28V. The 3V3 pin is a power output.
