# Fritzing sketch circuit v3 (saved by Fritzing 0.9.3b)
breadboards: 1

parts:
  Raspberry_Pi_1 = Raspberry Pi 3 [part_number=RPI-3-V1.2]
  2x_18650_(7_4v) = 18650 battery holder [package=battery-18650-kit]
  DC-_5v_DC = RioRand LM2596
  5v_3A = Header 2 [package=screwterminal-3.5mm-2_lock]
  PAN = Basic Servo
  TILT = Basic Servo
  MOTION_SW = SWITCH-DPDT [package=eg2211]
  Motion_Sns = RCWL-0516 Microwave Radar Motion Sensor Module
  U1 = RELAY [package=relay-jzc]
  Q1 = NPN-Transistor [package="TO92 [THT]"]
  R1 = Resistor [tolerance=±5% resistance=330 package="2010 [SMD]"]
  M1 = Stepper Motor - Bipolar
  M2 = Stepper Motor - Bipolar  # not connected
  U2 = L9110 H-bridge module [part_number="L9110 H-bridge"]

nets:
  3V3: Raspberry_Pi_1.3v3, Raspberry_Pi_1.3V3, MOTION_SW.1
  N1: Raspberry_Pi_1.GPIO2, Q1.B, R1.Pin_0
  N2: Raspberry_Pi_1.GPIO3, MOTION_SW.2
  GND: Raspberry_Pi_1.GND, DC-_5v_DC.Pin_4, 5v_3A.2, PAN.gnd, TILT.gnd, Motion_Sns.GND, Q1.C, U2.GND
  N3: Raspberry_Pi_1.GPIO17, PAN.pulse
  N4: Raspberry_Pi_1.GPIO27, TILT.pulse
  N5: Raspberry_Pi_1.GPIO6, U2.A-IA
  N6: Raspberry_Pi_1.GPIO13, U2.A-IB
  N7: Raspberry_Pi_1.GPIO19, U2.B-IA
  N8: Raspberry_Pi_1.GPIO26, U2.B-IB
  N9: Raspberry_Pi_1.5V, 5v_3A.1, U1.COIL2, R1.Pin_1
  N10: 2x_18650_(7_4v).+, U1.NO
  N11: 2x_18650_(7_4v).-, DC-_5v_DC.Pin_2
  N12: DC-_5v_DC.Pin_1, U1.MAIN
  VCC: DC-_5v_DC.Pin_3, PAN.vcc, TILT.vcc, Motion_Sns.VIN, U2.VCC
  N13: MOTION_SW.3, Motion_Sns.OUT
  N14: U1.COIL1, Q1.E
  N15: M1.A, U2.MOTOR_A-A
  N16: M1.C, U2.MOTOR_A-B
  N17: M1.B, U2.MOTOR_B-A
  N18: M1.D, U2.MOTOR_B-B

notes:
  V3.0 2019-09-08
  MVP
  In reality this module required input pin to GND to trigger, so the circuitry follows that logic.

custom parts:
  18650 battery holder: 18650 Battery Holder
  RCWL-0516 Microwave Radar Motion Sensor Module: The RCWL-0516 is a microwave radar motion sensor module. Input voltage is 4V to 28V. The 3V3 pin is a power output.
