# Fritzing sketch circuit v1_0 (saved by Fritzing 0.9.3b)
breadboards: 1

parts:
  Raspberry_Pi_1 = Raspberry Pi 3 [part_number=RPI-3-V1.2]
  TP1 = TP4056 [chip_label=TP4056 package="DIP (Dual Inline) [THT]"]
  BAT1 = 18650 battery holder [package=battery-18650-kit]
  TP2 = TP4056 [chip_label=TP4056 package="DIP (Dual Inline) [THT]"]
  BAT2 = 18650 battery holder [package=battery-18650-kit]
  M1 = RioRand LM2596
  7_4v_mains = Header 2 [package=screwterminal-3.5mm-2_lock]
  S1 = SWITCH-DPDT [package=eg2211]
  LED1 = RGB LED (com. cathode, rgb) [package="5 mm [THT]"]
  J1 = Basic Servo
  J2 = Basic Servo
  J3 = Basic Servo
  RCWL-0516_Microwave_Radar_Motion_Sensor1 = RCWL-0516 Microwave Radar Motion Sensor Module
  S2 = SWITCH-DPDT [package=eg2211]

nets:
  3V3: Raspberry_Pi_1.3v3, Raspberry_Pi_1.3V3, S2.3
  GND: Raspberry_Pi_1.GND, TP2.pin2, M1.Pin_4, LED1.common_cathode, RCWL-0516_Microwave_Radar_Motion_Sensor1.GND
  N1: Raspberry_Pi_1.GPIO21, J1.pulse
  N2: Raspberry_Pi_1.GPIO20, J2.pulse
  N3: Raspberry_Pi_1.GPIO16, J3.pulse
  N4: Raspberry_Pi_1.GPIO25, S2.2, S2.5
  N5: Raspberry_Pi_1.GPIO24, LED1.red_anode
  N6: Raspberry_Pi_1.GPIO23, LED1.green_anode
  N7: Raspberry_Pi_1.GPIO18, LED1.blue_anode
  5V: Raspberry_Pi_1.5V, M1.Pin_3, S1.2, RCWL-0516_Microwave_Radar_Motion_Sensor1.VIN
  N8: TP1.pin1, S1.3
  N9: TP1.pin2, TP2.pin1
  N10: TP1.pin3, TP2.pin3, S1.5
  N11: TP1.pin4, BAT1.+
  N12: TP1.pin5, BAT1.-
  GND_2: TP1.pin6, TP2.pin6, M1.Pin_2, 7_4v_mains.1, J1.gnd, J2.gnd, J3.gnd
  N13: TP2.pin4, BAT2.+
  N14: TP2.pin5, BAT2.-
  VCC: M1.Pin_1, 7_4v_mains.2, S1.4, J1.vcc, J2.vcc, J3.vcc
  N15: RCWL-0516_Microwave_Radar_Motion_Sensor1.OUT, S2.6

custom parts:
  TP4056: A DIP stand-in part for whatever IC you want. With 6 pins on a 300mil dual inline package (DIP) footprint.
  18650 battery holder: 18650 Battery Holder
  RCWL-0516 Microwave Radar Motion Sensor Module: The RCWL-0516 is a microwave radar motion sensor module. Input voltage is 4V to 28V. The 3V3 pin is a power output.
