# Fritzing sketch Lower Feb 2021 (saved by Fritzing 0.9.3b)
circuit board: 5.57377cm x 5.54779cm
breadboards: 1

parts:
  Serial = double row male pin header, 2 pins [form="♂ (male)"]
  Pi_PWR = double row male pin header, 2 pins [form="♂ (male)"]
  Srv1 = male pin header, 3 pins [form="♂ (male)"]
  Arduino_Pro_Mini = Arduino Pro Mini V2 (5V)
  5v = Mini-360 DC-DC Buck converter [package=THT]
  5_1v_Pi = Mini-360 DC-DC Buck converter [package=THT]
  J1 = female pin header, 3 pins [form="♀ (female)"]
  Srv_Pwr_Relay = female pin header, 3 pins [form="♀ (female)"]
  Srv2 = male pin header, 3 pins [form="♂ (male)"]
  Srv3 = male pin header, 3 pins [form="♂ (male)"]
  Srv4 = male pin header, 3 pins [form="♂ (male)"]
  Srv5 = male pin header, 3 pins [form="♂ (male)"]
  Srv6 = male pin header, 3 pins [form="♂ (male)"]
  Srv7 = male pin header, 3 pins [form="♂ (male)"]
  Srv8 = male pin header, 3 pins [form="♂ (male)"]
  Srv9 = male pin header, 3 pins [form="♂ (male)"]
  PWR = female pin header, 2 pins [form="♀ (female)"]
  FUSE = female pin header, 2 pins [form="♀ (female)"]
  Mon = female pin header, 2 pins [form="♀ (female)"]
  R1 = Resistor [tolerance=±5% resistance=220 package=THT]
  R2 = Resistor [tolerance=±5% resistance=220 package=THT]

nets:
  N1: Serial.pin1, Arduino_Pro_Mini.TXO
  N2: Serial.pin2, Arduino_Pro_Mini.RXI
  N3: Pi_PWR.pin1, 5_1v_Pi.OUT+
  N4: Pi_PWR.pin2, 5_1v_Pi.OUT-
  N5: Srv1.pin1, Arduino_Pro_Mini.D2
  N6: Srv1.pin2, J1.pin2, Srv2.pin2, Srv3.pin2, Srv4.pin2, Srv5.pin2, Srv6.pin2, Srv7.pin2, Srv8.pin2, Srv9.pin2
  N7: Srv1.pin3, Arduino_Pro_Mini.GND, 5v.OUT-, Srv_Pwr_Relay.pin2, Srv2.pin3, Srv3.pin3, Srv4.pin3, Srv5.pin3, Srv6.pin3, Srv7.pin3, Srv8.pin3, Srv9.pin3
  N8: Arduino_Pro_Mini.VCC, 5v.OUT+, J1.pin3, Srv_Pwr_Relay.pin1
  N9: Arduino_Pro_Mini.A0, R1.Pin_0, R2.Pin_1
  N10: Arduino_Pro_Mini.MOSI, Srv_Pwr_Relay.pin3
  N11: Arduino_Pro_Mini.D10, Srv9.pin1
  N12: Arduino_Pro_Mini.D9, Srv8.pin1
  N13: Arduino_Pro_Mini.D8, Srv7.pin1
  N14: Arduino_Pro_Mini.D7, Srv6.pin1
  N15: Arduino_Pro_Mini.D6, Srv5.pin1
  N16: Arduino_Pro_Mini.D5, Srv4.pin1
  N17: Arduino_Pro_Mini.D4, Srv3.pin1
  N18: Arduino_Pro_Mini.D3, Srv2.pin1
  N19: 5v.IN-, 5_1v_Pi.IN-, PWR.pin1, Mon.pin1, R1.Pin_1
  N20: 5v.IN+, 5_1v_Pi.IN+, FUSE.pin2, Mon.pin2, R2.Pin_0
  N21: PWR.pin2, FUSE.pin1

custom parts:
  Arduino Pro Mini V2 (5V): Arduino Pro Mini V2 There are several different layouts for this board out there. This one is modeled after the Sparkfun 11113 board but a few of the pins have been moved around.
  Mini-360 DC-DC Buck converter: Mini-360 DC-DC Buck converter. Tiny buck step down voltage converter, input voltage 4.75 to 23V output 1 to 17V adjustable. Available from ebay and the like.
