# Fritzing sketch body (saved by Fritzing 0.9.6b)
circuit board: 3.91202cm x 4.7976cm
breadboards: 1

parts:
  ProMini = Arduino Pro Mini v13
  D2 = Dagu DGServo 9g header (male) [package=THT]
  D6 = Dagu DGServo 9g header (male) [package=THT]
  D11 = Dagu DGServo 9g header (male) [package=THT]
  D9 = Dagu DGServo 9g header (male) [package=THT]
  D10 = Dagu DGServo 9g header (male) [package=THT]
  R1 = Resistor [tolerance=±2% power=0.25 resistance=330 package=THT]
  A0 = Resistor [tolerance=±2% power=0.25 resistance=330 package=THT]
  D3 = Dagu DGServo 9g header (male) [package=THT]
  D4 = Dagu DGServo 9g header (male) [package=THT]
  D5 = Dagu DGServo 9g header (male) [package=THT]
  D7 = Dagu DGServo 9g header (male) [package=THT]
  D8 = Dagu DGServo 9g header (male) [package=THT]
  5v+ = female pin header, 3 pins [form="♀ (female)"]
  Part1 = InvenSense MPU6050
  Bridge = female pin header, 2 pins [form="♀ (female)"]
  Pi = female pin header, 4 pins [form="♀ (female)"]
  vout = female pin header, 2 pins [form="♀ (female)"]

nets:
  N1: ProMini.D0/TX, Pi.pin4
  N2: ProMini.D1/RX, Pi.pin3
  VCC: ProMini.VCC, Part1.VCC, Bridge.pin1
  GND: ProMini.GND, D2.gnd, D6.gnd, D11.gnd, D9.gnd, D10.gnd, R1.Pin_0, D3.gnd, D4.gnd, D5.gnd, D7.gnd, D8.gnd, 5v+.pin2, Part1.GND, Pi.pin2, vout.pin2
  N3: ProMini.A4, Part1.SDA
  N4: ProMini.A5, Part1.SCL
  N5: ProMini.A0, R1.Pin_1, A0.Pin_1
  N6: ProMini.D11_PWM/MOSI, D11.pulse
  N7: ProMini.D10_PWM/SS, D10.pulse
  N8: ProMini.D9_PWM, D9.pulse
  N9: ProMini.D8, D8.pulse
  N10: ProMini.D7, D7.pulse
  N11: ProMini.D6_PWM, D6.pulse
  N12: ProMini.D5_PWM, D5.pulse
  N13: ProMini.D4, D4.pulse
  N14: ProMini.D3_PWM, D3.pulse
  N15: ProMini.D2, D2.pulse
  VCC_2: D2.Vcc, D6.Vcc, D11.Vcc, D9.Vcc, D10.Vcc, D3.Vcc, D4.Vcc, D5.Vcc, D7.Vcc, D8.Vcc, 5v+.pin3, Bridge.pin2
  N16: A0.Pin_0, 5v+.pin1, Pi.pin1, vout.pin1

notes:
  dan.makes.things v3.2
