# Fritzing sketch circuit (saved by Fritzing 0.9.3b)
breadboards: 1

parts:
  Raspberry_Pi_1 = Raspberry Pi 3 [part_number=RPI-3-V1.2]
  18650_(3_6v) = 18650 battery holder [package=battery-18650-kit]
  DC-_5v_DC = RioRand LM2596
  5v_3A = Header 2 [package=screwterminal-3.5mm-2_lock]
  UPPER_NECK = Basic Servo
  LOWER_NECK = Basic Servo
  Motion_Sns = RCWL-0516 Microwave Radar Motion Sensor Module
  Logic_Lvl = I2C level shifter bidirectional
  LEDs = WS2812 RGB LED matrix 1x8
  Arduino = Arduino Nano (Rev3.0) (ICSP)
  HEAD = Basic Servo
  Amp = LM4871 [package=so08]
  SP1 = SPEAKER [package=pcb_mount_speaker]
  S1 = Round Pushbutton
  Amp_Toggle = NPN-Transistor [package="TO92 [THT]"]
  Audio_Socket = 3.5mm Audio Jack [package=audio-jack-3.5mm-smd]

nets:
  3V3: Raspberry_Pi_1.3v3, Raspberry_Pi_1.3V3, Logic_Lvl.LV
  N1: Raspberry_Pi_1.GPIO3, S1.leg1
  GND: Raspberry_Pi_1.GND, DC-_5v_DC.Pin_4, 5v_3A.2, UPPER_NECK.gnd, LOWER_NECK.gnd, Motion_Sns.GND, Logic_Lvl.GND, LEDs.GND, Arduino.GND, HEAD.gnd, Amp.GND, S1.leg0
  N2: Raspberry_Pi_1.GPIO12, Motion_Sns.OUT
  N3: Raspberry_Pi_1.GPIO15, Logic_Lvl.LV2
  N4: Raspberry_Pi_1.GPIO14, Logic_Lvl.LV1
  5V: Raspberry_Pi_1.5V, 5v_3A.1, Motion_Sns.VIN
  N5: 18650_(3_6v).+, DC-_5v_DC.Pin_1
  N6: 18650_(3_6v).-, DC-_5v_DC.Pin_2
  VCC: DC-_5v_DC.Pin_3, UPPER_NECK.vcc, LOWER_NECK.vcc, Logic_Lvl.HV, LEDs.VCC, Arduino.5V, HEAD.vcc, Amp_Toggle.C
  N7: UPPER_NECK.pulse, Arduino.D4
  N8: LOWER_NECK.pulse, Arduino.D5
  N9: Logic_Lvl.HV1, Arduino.D0/RX
  N10: Logic_Lvl.HV2, Arduino.D1/TX
  N11: LEDs.DIN, Arduino.D13/SCK
  N12: Arduino.D3, HEAD.pulse
  N13: Arduino.D12/MISO, Amp_Toggle.B
  N14: Amp.IN+, Audio_Socket.LEFT
  N15: Amp.IN-, Audio_Socket.SLEEVE
  N16: Amp.V01, SP1.-
  N17: Amp.VDD, Amp_Toggle.E
  N18: Amp.V02, SP1.+

notes:
  V3.0 2019-12-21

custom parts:
  18650 battery holder: 18650 Battery Holder
  RCWL-0516 Microwave Radar Motion Sensor Module: The RCWL-0516 is a microwave radar motion sensor module. Input voltage is 4V to 28V. The 3V3 pin is a power output.
  WS2812 RGB LED matrix 1x8: WS2812 matrix 1x8
