# Fritzing sketch mains only circuit v1 (saved by Fritzing 0.9.3b)
breadboards: 1

parts:
  Raspberry_Pi_1 = Raspberry Pi 3 [part_number=RPI-3-V1.2]
  POW_SW = SWITCH-DPDT [package=eg2211]
  RGB_LED = RGB LED (com. cathode, rgb) [package="5 mm [THT]"]
  PAN = Basic Servo
  TILT = Basic Servo
  BOUNCE = Basic Servo
  MOTION_SW = SWITCH-DPDT [package=eg2211]
  Motion_Sns = RCWL-0516 Microwave Radar Motion Sensor Module
  5v_mains = Header 2 [package=screwterminal-3.5mm-2_lock]
  C1 = Capacitor Polarized [package=cpol-radial-100uf-25v]

nets:
  3V3: Raspberry_Pi_1.3v3, Raspberry_Pi_1.3V3, MOTION_SW.1
  N1: Raspberry_Pi_1.GPIO3, MOTION_SW.2
  GND: Raspberry_Pi_1.GND, RGB_LED.common_cathode, PAN.gnd, TILT.gnd, BOUNCE.gnd, Motion_Sns.GND, 5v_mains.1, C1.-
  N2: Raspberry_Pi_1.GPIO17, PAN.pulse
  N3: Raspberry_Pi_1.GPIO27, TILT.pulse
  N4: Raspberry_Pi_1.GPIO22, BOUNCE.pulse
  N5: Raspberry_Pi_1.GPIO5, RGB_LED.blue_anode
  N6: Raspberry_Pi_1.GPIO6, RGB_LED.green_anode
  N7: Raspberry_Pi_1.GPIO13, RGB_LED.red_anode
  VCC: Raspberry_Pi_1.5V, POW_SW.5, PAN.vcc, TILT.vcc, BOUNCE.vcc, Motion_Sns.VIN, C1.+
  N8: POW_SW.4, 5v_mains.2
  N9: MOTION_SW.3, Motion_Sns.OUT

notes:
  V1.0 2019-06-25

custom parts:
  RCWL-0516 Microwave Radar Motion Sensor Module: The RCWL-0516 is a microwave radar motion sensor module. Input voltage is 4V to 28V. The 3V3 pin is a power output.
